# Fritzing sketch esquema_montaje (saved by Fritzing 1.0.1rc)
breadboards: 1

parts:
  Componente1 = Arduino Nano (Rev3.0)
  Componente2 = iceZUM Alhambra
  S1 = 0.91 inch OLED I2C Display 128 x 32 Pixels
  J1 = Piezo Speaker
  M2 = Dagu DGServo 9g (Pan and tilt) [part_number=RS001B]

nets:
  GND: Componente1.GND, S1.GND
  5V: Componente1.5V, S1.VCC
  N1: Componente1.A5, S1.SCL
  N2: Componente1.A4, S1.SDA
  N3: Componente2.D3, Componente2.V3#56, M2.pulse
  N4: Componente2.G3, M2.gnd
  N5: Componente2.G0, J1.pin1
  N6: Componente2.V3#42, M2.vcc
  N7: Componente2.V0, J1.pin2

custom parts:
  iceZUM Alhambra: Arduino/zum compatible Open FPGA electronic board. Synthesize hardware easily, using only open source tools
